# Fritzing sketch InvertorIc (saved by Fritzing 0.8.7b)
breadboards: 1

parts:
  Part1 = Arduino Uno (Rev3)
  U1 = 74HC04_HEX_INVERTER [package=dil14]
  LED1 = LED - 5mm [color="Red (633nm)" package="5 mm [THT]"]
  LED2 = LED - 5mm [color="Red (633nm)" package="5 mm [THT]"]
  R1 = Resistor [tolerance=±5% resistance=220 package=THT]

nets:
  N1: Part1.D13/SCK, U1.1A, LED1.anode
  5V: Part1.5V, U1.VCC
  GND: Part1.GND, U1.GND, R1.Pin_1
  N2: U1.1Y, LED2.anode
  N3: LED1.cathode, LED2.cathode, R1.Pin_0

notes:
  Left LED will light up if 13 is HIGH
  Right LED will light up if 13 is LOW,
  as the LOW 13 gets inverted to HIGH
  Upload Blink
