# Fritzing sketch InverterTransistors (saved by Fritzing 0.8.7b)
circuit board: 10cm x 8cm
breadboards: 1

parts:
  Part1 = Arduino Uno (Rev3)
  RLED2 = Resistor [tolerance=±5% resistance=1k package=THT]
  LED2 = LED - 5mm [color="Red (633nm)" package="5 mm [THT]"]
  D1 = Rectifier Diode [part_number=1N4001 package="300 mil [THT]"]
  R1 = Resistor [tolerance=±5% resistance=1k package=THT]
  R2 = Resistor [tolerance=±5% resistance=1k package=THT]
  R4 = Resistor [tolerance=±5% resistance=1k package=THT]
  R3 = Resistor [tolerance=±5% resistance=1k package=THT]
  D2 = Rectifier Diode [part_number=1N4001 package="300 mil [THT]"]
  LED1 = LED - 5mm [color="Red (633nm)" package="5 mm [THT]"]
  RLED1 = Resistor [tolerance=±5% resistance=1k package=THT]
  Q1 = NPN-Transistor [package="TO92 [THT]"]
  Q2 = NPN-Transistor [package="TO92 [THT]"]
  Q3 = NPN-Transistor [package="TO92 [THT]"]
  Q4 = NPN-Transistor [package="TO92 [THT]"]
  J = female pin header, 3 pins [form="♀ (female)"]
  part = NPN-Transistor [package="TO92 [THT]"]  # not connected

nets:
  N1: Part1.D2, LED2.anode, D1.cathode, Q1.E, J.pin2
  N2: Part1.5V, R1.Pin_1, R2.Pin_1, R4.Pin_1, J.pin1
  N3: Part1.GND, RLED2.Pin_1, D1.anode, R3.Pin_1, D2.cathode, LED1.anode, RLED1.Pin_1, Q4.E, Q4.C, J.pin3
  N4: RLED2.Pin_0, LED2.cathode
  N5: R1.Pin_0, Q1.B
  N6: R2.Pin_0, Q2.E, Q4.B
  N7: R4.Pin_0, Q3.C
  N8: R3.Pin_0, Q2.C, Q3.B
  N9: D2.anode, Q3.E
  N10: LED1.cathode, RLED1.Pin_0
  N11: Q1.C, Q2.B

notes:
  Should emit when input is low
  Header pins:
  1) +5V
  2) signal
  3) 0V
  Should emit when input is high
